# Fritzing sketch trafficLight (saved by Fritzing 0.9.3b)
breadboards: 1

parts:
  Raspberry_Pi1 = Raspberry Pi 2
  LED1 = LED - 5mm [color="Red (633nm)" package="5 mm [THT]"]
  R1 = Resistor [tolerance=±5% resistance=330k package=THT]
  LED2 = LED - 5mm [color="Yellow (585nm)" package="5 mm [THT]"]
  R2 = Resistor [tolerance=±5% resistance=560 package=THT]
  LED3 = LED - 5mm [color="Green (560nm)" package="5 mm [THT]"]
  R3 = Resistor [tolerance=±5% resistance=560 package=THT]
  LED4 = LED - 5mm [color="Red (633nm)" package="5 mm [THT]"]
  LED5 = LED - 5mm [color="Green (555nm)" package="5 mm [THT]"]
  R4 = Resistor [tolerance=±5% resistance=330 package=THT]
  R5 = Resistor [tolerance=±5% resistance=560 package=THT]

nets:
  N1: Raspberry_Pi1.3v3, R1.Pin_1, R2.Pin_1, R3.Pin_1, R4.Pin_1, R5.Pin_1
  N2: Raspberry_Pi1.GPIO17, LED4.cathode
  N3: Raspberry_Pi1.GPIO22, LED5.cathode
  N4: Raspberry_Pi1.GPIO5, LED1.cathode
  N5: Raspberry_Pi1.GPIO6, LED2.cathode
  N6: Raspberry_Pi1.GPIO13, LED3.cathode
  N7: LED1.anode, R1.Pin_0
  N8: LED2.anode, R2.Pin_0
  N9: LED3.anode, R3.Pin_0
  N10: LED4.anode, R4.Pin_0
  N11: LED5.anode, R5.Pin_0
